# Fritzing sketch Shield (saved by Fritzing 0.9.5d)
breadboards: 1

parts:
  A1 = Raspberry Pi 5
  U1 = LCD-16X2 [package=lcd-16x2_noholes]
  Componente2 = Adafruit BME280 [part_number="Adafruit #2652"]
  LCD2004-I2C1 = LCD2004-I2C
  R1 = TRIMPOT [package=3362u-2]
  R2 = Resistor [tolerance=±5% resistance=220 package="1206 [SMD]"]
  LED1 = smd LED [color="Red (633nm)" package="0603 [SMD]"]

nets:
  GND: A1.GND, U1.VSS, U1.R_W, U1.K, R1.CW, R2.Pin_1
  N1: A1.GPIO17, LED1.anode
  N2: A1.GPIO18, U1.DB7
  N3: A1.GPIO27, U1.A
  N4: A1.GPIO23, U1.DB6
  N5: A1.GPIO24, U1.DB5
  N6: A1.GPIO25, U1.DB4
  N7: A1.GPIO8, U1.E
  N8: A1.GPIO7, U1.RS
  N9: U1.VDD, R1.CCW
  N10: U1.VO, R1.WIPER
  VCC: Componente2.VCC, LCD2004-I2C1.VCC
  GND_2: Componente2.GND, LCD2004-I2C1.GND
  N11: Componente2.SCK/SCL, LCD2004-I2C1.SCL
  N12: Componente2.SDI/SDA, LCD2004-I2C1.SDA
  N13: R2.Pin_0, LED1.cathode

custom parts:
  Raspberry Pi 5: The RPi5, a faster version of the awesome Raspberry Pi4B ARM Board with 40 pin gpio.
  Adafruit BME280: Bosch has stepped up their game with their new BME280 sensor, an environmental sensor with temperature, barometric pressure and humidity! This sensor is great for all sorts of indoor environmental sensing and can even be used in both I2C and SPI! This precision sensor from Bosch is the best low-cost sensing solution for measuring humidity with ±3% accuracy, barometric pressure with ±1 hPa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
  LCD2004-I2C: A standard character display with 4x20 characters. Comes in many colors with LCM2004 IIC attached.
